# Fritzing sketch SmarterTVRadio (saved by Fritzing 0.9.3b)
breadboards: 1

parts:
  U1 = ESP8266 NodeMCU LoLin module
  IR3 = TSOP312.., 314.. [package=THT]
  LED1 = LED - 5mm [color="Infrared (850nm)" package="5 mm [THT]"]
  R1 = Resistor [tolerance=±0.1% resistance=220 package=THT]

nets:
  N1: U1.D2, LED1.anode
  N2: U1.D3, IR3.Data
  N3: U1.3V3, IR3.Vs
  GND: U1.GND, IR3.GND, R1.Pin_1
  N4: LED1.cathode, R1.Pin_0

custom parts:
  ESP8266 NodeMCU LoLin module: ESP8266 based NodeMCU

// code stored in the sketch: MQTTNodeMCU.ino
/*
 Name:		NodeMCU.ino
 Created:	28.06.2019 17:00:15
 Author:	kiefe
*/




#include <ESP8266WiFi.h>
#include <PubSubClient.h>

#include <IRremoteESP8266.h>
#include <IRrecv.h>
#include <IRutils.h>
#include <IRsend.h>
#include <stdlib.h>


const char* ssid = "Gustav";
const char* pass = "!Gorky_Y3";
const char* ip = "192.168.178.52";

int recievePin = D3;

IRsend irsend(4);

IRrecv irrecv(recievePin);
decode_results results;

WiFiClient wifiClient;
PubSubClient client(wifiClient);
long lastMsg = 0;
char msg[50];
int value = 0;

void setup_wifi() {
	delay(10);

	Serial.println();
	Serial.print("Connecting to ");
	Serial.println(ssid);

	WiFi.begin(ssid, pass);

	while (WiFi.status() != WL_CONNECTED){
		delay(500);
		Serial.print(".");
	}

	Serial.println();
	Serial.println("WiFi coonnected");
	Serial.print("IP address: ");
	String locIP = WiFi.localIP().toString();
	Serial.println(locIP);
}

void callback(char* topic, byte* payload, unsigned int length) {
	String message = "";
	Serial.print("Message arrived [");
	Serial.print(topic);
	Serial.println("]");

	for (int i = 0; i < length; i++) {
		message = message + (char)payload[i];
	}

	//if (topic == "irSend") {
    int sendCode = message.toInt();
    Serial.print(sendCode);
		irsend.sendRC5(sendCode);
		Serial.println("sending Signal");
	//}

	Serial.println(message);
}

void reconnect() {
	while (!client.connected()) {
		Serial.print("Attempting MQTT connection...");
		// Create a random client ID
		String clientId = "ESP8266Client-";
		clientId += String(random(0xffff), HEX);
		if (client.connect(clientId.c_str())) {
			Serial.println("connected");
			// Once connected, publish an announcement...
			client.publish("outTopic", "hello world");
			// ... and resubscribe
			client.subscribe("inTopic");
			client.subscribe("irSend");
		} else {
			Serial.print("failed, rc=");
			Serial.print(client.state());
			Serial.println(" try again in 5 seconds");
			// Wait 5 seconds before retrying
			delay(5000);
		}
	}
}

// the setup function runs once when you press reset or power the board
void setup() {
	pinMode(BUILTIN_LED, OUTPUT);
	pinMode(4, OUTPUT);
	digitalWrite(4, HIGH);
	delay(1000);
	digitalWrite(4, LOW);
	Serial.begin(115200);
	Serial.println("Starting Wifi-Setup");
	setup_wifi();
	client.setServer(ip, 1883);
	client.setCallback(callback);
	irrecv.enableIRIn();
}

// the loop function runs over and over again until power down or reset
void loop() {

	if (!client.connected()) {
		reconnect();
	}
	client.loop();

	if (irrecv.decode(&results)) {
		String type = typeToString(results.decode_type);
		String val = uint64_tToHex(results.value);
		String message = String("Recieved on " + type);
		message += ": ";
		message += val;
		Serial.println(message);
		client.publish("irOut", message.c_str());
		delay(5);
		irrecv.resume();
	}

	/*long now = millis();
	if (now - lastMsg > 2000) {
		lastMsg = now;
		++value;
		snprintf(msg, 50, "hello world #%1d", value);
		Serial.print("Publish message: ");
		Serial.println(msg);
		client.publish("outTopic", msg);
	}*/

}

String uint64_tToHex(uint64_t uint) {
	char buffer[100];
	sprintf(buffer, "0x%x", uint);
	String hexString = buffer;
	return(hexString);
}

uint64_t hexToUint64_t(String hexStr){
  const char* buffer = hexStr.c_str();
  int uint = 0;
  uint = (int) strtol( &hexStr[1], NULL, 16);
  return uint;
  Serial.print(uint);
}
